# Fritzing sketch Alchemy Machine (saved by Fritzing 0.9.9b)
breadboards: 1

parts:
  MH-ET_LIVE_ESP32_DEVKIT1 = MH-ET LIVE ESP32 DEVKIT 38 pins
  L1 = MagLock
  Mod1 = KY-019 5V Relay Module [package="Breakout board"]
  U1 = WS2812 RGB LED strip
  Part3 = VERTER 5V USB Buck-Boost
  Part4 = TXB0104 4-channel Bi-Directional Level Shifter
  Mod2 = KY-019 5V Relay Module [package="Breakout board"]
  L2 = MagLock
  Mod3 = laser receiver [package=THT]
  U2 = WS2812 RGB LED strip
  U3 = WS2812 RGB LED strip
  U4 = WS2812 RGB LED strip
  Part5 = PN5180-NFC
  Part6 = PN5180-NFC
  LimitSwitch = SPST Switch [package=switch-spdt]
  BAT1 = 12 battery [package=battery]

nets:
  N1: MH-ET_LIVE_ESP32_DEVKIT1.3V3, Part4.LV
  N2: MH-ET_LIVE_ESP32_DEVKIT1.IO34, Mod3.pin2
  N3: MH-ET_LIVE_ESP32_DEVKIT1.IO35, LimitSwitch.P
  N4: MH-ET_LIVE_ESP32_DEVKIT1.IO32, Mod2.S
  N5: MH-ET_LIVE_ESP32_DEVKIT1.IO33, Mod1.S
  N6: MH-ET_LIVE_ESP32_DEVKIT1.IO25, Part4.A1
  N7: MH-ET_LIVE_ESP32_DEVKIT1.IO26, Part4.A2
  N8: MH-ET_LIVE_ESP32_DEVKIT1.IO27, Part4.A3
  N9: MH-ET_LIVE_ESP32_DEVKIT1.GND#58, LimitSwitch.S
  N10: MH-ET_LIVE_ESP32_DEVKIT1.IO13, Part4.A4
  VCC: MH-ET_LIVE_ESP32_DEVKIT1.5V, Mod1.+, U1.VCC, Part3.5.0V, Part4.HV, Mod2.+, Mod3.pin3, U2.VCC, U3.VCC, U4.VCC, Part6.5V
  N11: MH-ET_LIVE_ESP32_DEVKIT1.IO23, Part5.MOSI
  N12: MH-ET_LIVE_ESP32_DEVKIT1.IO22, Part5.RST
  N13: MH-ET_LIVE_ESP32_DEVKIT1.IO21, Part5.NSS
  GND: MH-ET_LIVE_ESP32_DEVKIT1.GND#70, L1.pin1, Mod1.-, U1.GND, Part3.GND, Part4.GND, Part4.OE, Mod2.-, L2.pin1, Mod3.pin1, U2.GND, U3.GND, U4.GND, Part6.GND, BAT1.-
  N14: MH-ET_LIVE_ESP32_DEVKIT1.IO19, Part5.MISO
  N15: MH-ET_LIVE_ESP32_DEVKIT1.IO18, Part5.SCK
  N16: MH-ET_LIVE_ESP32_DEVKIT1.IO5, Part5.BUSY
  N17: MH-ET_LIVE_ESP32_DEVKIT1.IO17, Part6.RST
  N18: MH-ET_LIVE_ESP32_DEVKIT1.IO16, Part6.NSS
  N19: MH-ET_LIVE_ESP32_DEVKIT1.IO4, Part6.BUSY
  N20: L1.pin2, Mod1.NO
  N21: Mod1.Common, Part3.VIN, Mod2.Common, BAT1.+
  N22: U1.DIN, Part4.B1
  N23: Part4.B2, U2.DIN
  N24: Part4.B3, U3.DIN
  N25: Part4.B4, U4.DIN
  N26: Mod2.NO, L2.pin2

notes:
  Limit Switch
  Buck Converter 12V -> 5V
  CrystalDoor Relay
  BeakerDoor Lock (momentary high to release lock)
  CrystalDoor Maglock
  LS1
  LS2
  LS3
  Laser Sensor
  LS4
  Logic Level Converter
  HV = 5V
  LV = 3.3V
  nfc[0]
  nfc[1]
  5V Power Rail
  12V Power Rail
  12V Power Supply

custom parts:
  MH-ET LIVE ESP32 DEVKIT 38 pins: http://mh.nodebb.com/topic/2/mh-et-live-esp32-devkit
  MagLock: A bar-style 12V/24V maglock
  KY-019 5V Relay Module: KY-019 5V Relay module, used to control AC circuits. (Special thanks to vanepp for fixing the PCB holes and other errors)
  WS2812 RGB LED strip: WS2812 strip
  VERTER 5V USB Buck-Boost: VERTER can take battery voltages from 3-12VDC and output a nice 5V DC, which makes it a perfect universal power supply for your portable project! Where Verter really shines is when you have a battery or power range that can fluctuate a lot, or you don't know what you'll end up using.
  TXB0104 4-channel Bi-Directional Level Shifter: Because the Arduino (and Basic Stamp) are 5V devices, and most modern sensors, displays, flash cards and modes are 3.3V-only, many makers find that they need to perform level shifting/conversion to protect the 3.3V device from 5V. Although one can use resistors to make a divider, for high speed transfers, the resistors can add a lot of slew and cause havoc that is tough to debug. For that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
  laser receiver: Generic non modulated laser receiver module.
  PN5180-NFC: RFID High Frequency IC card reader/writer based on the PN5180 chip from NXP.
  12 battery: 12V lead acid type battery, like the Husqvarna YTH2448 12V 35AH battery. This is the mini version 1/4 the size of the actual battery to be closer to typical breadboard parts (around 2in wide rathher than 7in). The pads in pcb are sized to accomidate up to 14ga wire (as these batterys will deliver high currents.)
